# Fritzing sketch Server (saved by Fritzing 0.8.3b)
breadboards: 1

parts:
  Componente1 = Arduino Nano (Rev3.0)
  C1 = Tantalum Capacitor [capacitance="1 μF" package="100 mil [THT, tantalum]"]
  C2 = Electrolytic Capacitor [capacitance=1µF package="100 mil [THT, electrolytic]"]
  U1 = ESP8266 WiFi Module [part_number=ESP8266]
  IC1 = Voltage Regulator [package=to-220-alt]
  NRF24L2 = NRF24L01

nets:
  N1: Componente1.D1/TX, U1.RXD
  N2: Componente1.D0/RX, U1.TXD
  GND: Componente1.GND, C1.-, C2.-, U1.GND, IC1.GND
  N3: Componente1.D7, NRF24L2.CE
  N4: Componente1.D8, NRF24L2.CSN
  VIN: Componente1.D11/MOSI, Componente1.VIN, Componente1.5V, NRF24L2.MISO
  N5: Componente1.D12/MISO, Componente1.D13/SCK, NRF24L2.MOSI, NRF24L2.SCK
  N6: C1.+, C2.+, U1.VCC, U1.CH_PD, IC1.IN
  N7: IC1.OUT, NRF24L2.GND

custom parts:
  ESP8266 WiFi Module: Generic WiFi Module based on the ESP8266 with onboard PCB antenna and UART communications
  NRF24L01: NRF24L01 module
